# Fritzing sketch car (saved by Fritzing 0.9.1b)
circuit board: 7.03537cm x 5.42513cm
breadboards: 1

parts:
  Composant1 = Arduino Uno (Rev3)
  IC1 = L293D [package=THT]
  M2 = DC Motor
  R6 = Photocell (LDR) [package=THT]
  J4 = Piezo Speaker
  M1 = DC Motor
  V2 = DC Power [voltage=5]
  JP1 = USB_MICROB_PLUG [package=micro-b-th]
  LED2 = LED - 3mm [color="Red (633nm)" package="3 mm [THT]"]
  LED1 = LED - 3mm [color="Red (633nm)" package="3 mm [THT]"]
  LED4 = LED - 3mm [color="Yellow (592nm)" package="3 mm [THT]"]
  LED3 = LED - 3mm [color="Yellow (592nm)" package="3 mm [THT]"]
  C3 = Electrolytic Capacitor [capacitance=0.1mF package="100 mil [THT, electrolytic]"]
  C2 = Electrolytic Capacitor [capacitance=0.1mF package="100 mil [THT, electrolytic]"]
  C1 = Electrolytic Capacitor [capacitance=0.1mF package="100 mil [THT, electrolytic]"]
  R5 = Resistor [tolerance=±5% resistance=10k package=THT]
  R2 = Resistor [tolerance=±5% resistance=220 package=THT]
  R1 = Resistor [tolerance=±5% resistance=220 package=THT]
  R4 = Resistor [tolerance=±5% resistance=220 package=THT]
  R3 = Resistor [tolerance=±5% resistance=220 package=THT]
  Q1 = NPN-Transistor [package="TO92 [THT]"]
  J3 = Basic Servo
  J1 = Basic Servo
  J2 = Basic Servo

nets:
  N1: Composant1.A0, R6.pin_1, R5.Pin_0
  N2: Composant1.D8, IC1.In_4
  N3: Composant1.D9_PWM, IC1.Enable_2
  N4: Composant1.D10_PWM/SS, J1.pulse
  N5: Composant1.D11_PWM/MOSI, Q1.B
  N6: Composant1.D12/MISO, J4.pin2
  GND: Composant1.GND, IC1.0V, J4.pin1, V2.V-, JP1.GND, C3.-, C2.-, C1.-, R5.Pin_1, Q1.E, J3.gnd, J1.gnd, J2.gnd
  N7: Composant1.D2, IC1.In_2
  N8: Composant1.D3_PWM, IC1.Enable_1
  N9: Composant1.D4, IC1.In_1
  N10: Composant1.D5_PWM, J3.pulse
  N11: Composant1.D6_PWM, J2.pulse
  N12: Composant1.D7, IC1.In_3
  N13: Composant1.5V, R6.pin_0
  N14: Composant1.VIN, V2.V+
  N15: IC1.Out_1_(_Controlled_by_Enable_1_), M2.pin_2
  N16: IC1.Out_2_(_Controlled_by_Enable_1_), M2.pin_1
  VCC: IC1.+Vmotor, IC1.+V, JP1.VCC, LED2.anode, LED1.anode, LED4.anode, LED3.anode, C3.+, C2.+, C1.+, J3.vcc, J1.vcc, J2.vcc
  N17: IC1.Out_3_(_Controlled_by_Enable_2_), M1.pin_1
  N18: IC1.Out_4_(_Controlled_by_Enable_2_), M1.pin_2
  N19: LED2.cathode, R2.Pin_0
  N20: LED1.cathode, R1.Pin_0
  N21: LED4.cathode, R4.Pin_0
  N22: LED3.cathode, R3.Pin_0
  N23: R2.Pin_1, R1.Pin_1, R4.Pin_1, R3.Pin_1, Q1.C

notes:
  Car schematics v0.1
